# Fritzing sketch COUCOUrubanLED (saved by Fritzing 0.9.3b)

parts:
  LED1 = Super Flux RGB LED (com. anode) [color=Blue part_number=WS2812B]
  LED2 = Super Flux RGB LED (com. anode) [color=Blue part_number=WS2812B]
  LED3 = Super Flux RGB LED (com. anode) [color=Blue part_number=WS2812B]
  LED4 = Super Flux RGB LED (com. anode) [color=Blue part_number=WS2812B]
  LED5 = Super Flux RGB LED (com. anode) [color=Blue part_number=WS2812B]
  WeMos_D1_Mini1 = WeMos D1 Mini

nets:
  N1: LED1.blue_cathode, LED2.common_anode
  N2: LED1.green_cathode, LED5.green_cathode, WeMos_D1_Mini1.G
  N3: LED1.common_anode, WeMos_D1_Mini1.D4
  N4: LED2.blue_cathode, LED3.common_anode
  N5: LED3.blue_cathode, LED4.common_anode
  N6: LED4.blue_cathode, LED5.common_anode
